# Fritzing sketch LDR-BUZZER (saved by Fritzing 0.9.0b)
breadboards: 1

parts:
  R1 = Photocell (LDR) [package=THT]
  Componente1 = Arduino Uno (Rev3)
  R3 = Resistor [tolerance=±5% resistance=10k package=THT]
  J1 = Piezo Speaker
  R4 = Resistor [tolerance=±5% resistance=100 package=THT]

nets:
  N1: R1.pin_0, Componente1.5V
  N2: R1.pin_1, Componente1.A0, R3.Pin_0
  N3: Componente1.GND, R3.Pin_1, J1.pin1
  N4: Componente1.D3_PWM, R4.Pin_1
  N5: J1.pin2, R4.Pin_0

notes:
  10k ohm
  100 ohm
