# Fritzing sketch LDR-LED-2 (saved by Fritzing 0.9.0b)
breadboards: 1

parts:
  R1 = Photocell (LDR) [package=THT]
  LED1 = LED - 5mm [color="Red (633nm)" package="5 mm [THT]"]
  Componente1 = Arduino Uno (Rev3)
  R3 = Resistor [tolerance=±5% resistance=10k package=THT]
  R2 = Resistor [tolerance=±5% resistance=100 package=THT]

nets:
  N1: R1.pin_0, Componente1.5V
  N2: R1.pin_1, Componente1.A0, R3.Pin_0
  N3: LED1.cathode, Componente1.GND, R3.Pin_1
  N4: LED1.anode, Componente1.D13/SCK, R2.Pin_0, R2.Pin_1

notes:
  10k ohm
  100 ohm
