# Fritzing sketch montagem_banana (saved by Fritzing 0.9.3b)
breadboards: 1

parts:
  Arduino1 = Arduino
  LED1 = LED - 5mm [color="Red (633nm)" package="5 mm [THT]"]
  R1 = Resistor [tolerance=±5% resistance=220 package=THT]

nets:
  N1: Arduino1.D12, R1.Pin_1
  N2: Arduino1.GND, LED1.cathode
  N3: LED1.anode, R1.Pin_0
