# Fritzing sketch montagem_banana (saved by Fritzing 0.8.5b)
breadboards: 1

parts:
  LED1 = LED - 5mm [color="Red (633nm)" package="5 mm [THT]"]  # not connected
  R1 = Resistor [tolerance=±5% resistance=2.2k package=THT]
  Arduino1 = Arduino Uno (Rev3)
  J1 = Piezo Speaker
  R3 = Resistor [tolerance=±5% resistance=2.2k package=THT]

nets:
  N1: R1.Pin_1, Arduino1.D12/MISO
  N2: Arduino1.D9_PWM, R3.Pin_1
  N3: J1.pin2, R3.Pin_0
