# Fritzing sketch montagem_projeto_2-5 (saved by Fritzing 0.9.3b)
breadboards: 1

parts:
  LED1 = LED - 5mm [color="Red (633nm)" package="5 mm [THT]"]
  Arduino1 = Arduino Uno (Rev3)
  R6 = Resistor [tolerance=±5% resistance=100 package=THT]
  R7 = Rotary Potentiometer (Small) [maximum_resistance=100kΩ package=THT]

nets:
  N1: LED1.cathode, Arduino1.GND, R7.leg2
  N2: LED1.anode, R6.Pin_0
  N3: Arduino1.A0, R7.wiper
  N4: Arduino1.D12/MISO, R6.Pin_1
  N5: Arduino1.5V, R7.leg1
