# Fritzing sketch montagem_projeto_3 (saved by Fritzing 0.9.3b)
breadboards: 1

parts:
  LED1 = LED - 5mm [color="Red (633nm)" package="5 mm [THT]"]
  Arduino1 = Arduino Uno (Rev3)
  R6 = Resistor [tolerance=±5% resistance=100 package=THT]
  R10 = Resistor [tolerance=±5% resistance=100 package=THT]
  J1 = Piezo Speaker

nets:
  N1: LED1.cathode, Arduino1.GND, R10.Pin_1
  N2: LED1.anode, R6.Pin_0
  N3: Arduino1.D12/MISO, R6.Pin_1
  N4: Arduino1.D3_PWM, J1.pin2
  N5: R10.Pin_0, J1.pin1
