# Fritzing sketch montagem_projeto_4 (saved by Fritzing 0.8.5b)
breadboards: 1

parts:
  LED1 = LED - 5mm [color="Red (633nm)" package="5 mm [THT]"]
  Arduino1 = Arduino Uno (Rev3)
  J1 = Piezo Speaker  # not connected
  LED2 = LED - 5mm [color="Red (633nm)" package="5 mm [THT]"]
  LED3 = LED - 5mm [color="Red (633nm)" package="5 mm [THT]"]
  LED4 = LED - 5mm [color="Red (633nm)" package="5 mm [THT]"]
  LED5 = LED - 5mm [color="Red (633nm)" package="5 mm [THT]"]
  R5 = Resistor [tolerance=±5% resistance=100 package=THT]
  R6 = Resistor [tolerance=±5% resistance=100 package=THT]
  R7 = Resistor [tolerance=±5% resistance=100 package=THT]
  R8 = Resistor [tolerance=±5% resistance=100 package=THT]
  R9 = Resistor [tolerance=±5% resistance=100 package=THT]
  R10 = Resistor [tolerance=±5% resistance=100 package=THT]

nets:
  N1: LED1.cathode, Arduino1.GND, LED2.cathode, LED3.cathode, LED4.cathode, LED5.cathode
  N2: LED1.anode, R6.Pin_0
  N3: Arduino1.D8, R9.Pin_1
  N4: Arduino1.D9_PWM, R8.Pin_1
  N5: Arduino1.D10_PWM/SS, R5.Pin_1
  N6: Arduino1.D11_PWM/MOSI, R7.Pin_1
  N7: Arduino1.D12/MISO, R6.Pin_1
  N8: Arduino1.D3_PWM, R10.Pin_1
  N9: LED2.anode, R7.Pin_0
  N10: LED3.anode, R5.Pin_0
  N11: LED4.anode, R8.Pin_0
  N12: LED5.anode, R9.Pin_0
