# Fritzing sketch montagem_projeto_1 (saved by Fritzing 0.8.5b)
breadboards: 1

parts:
  LED1 = LED - 5mm [color="Red (633nm)" package="5 mm [THT]"]
  Arduino1 = Arduino Uno (Rev3)
  R6 = Resistor [tolerance=±5% resistance=100 package=THT]

nets:
  N1: LED1.cathode, Arduino1.GND
  N2: LED1.anode, R6.Pin_0
  N3: Arduino1.D12/MISO, R6.Pin_1
