# Fritzing sketch montagem_projeto_6 (saved by Fritzing 0.8.5b)
breadboards: 1

parts:
  Arduino1 = Arduino Uno (Rev3)
  J1 = Piezo Speaker  # not connected
  R10 = Resistor [tolerance=±5% resistance=100 package=THT]

nets:
  N1: Arduino1.D3_PWM, R10.Pin_1
