# Fritzing sketch oficina_automatizada (saved by Fritzing 0.9.3b)
breadboards: 1

parts:
  Part1 = Soil Moisture Sensor
  Part2 = Arduino Uno (Rev3) - ICSP
  WeMos_D1_Mini_Relay_Shield_V1 = WeMos D1 Mini Relay Shield V2
  L1 = Solenoid

nets:
  N1: Part1.SIG, Part2.A0
  GND: Part1.GND, Part2.GND, WeMos_D1_Mini_Relay_Shield_V1.G
  5V: Part1.VCC, Part2.5V, WeMos_D1_Mini_Relay_Shield_V1.5V
  N2: Part2.D4, WeMos_D1_Mini_Relay_Shield_V1.D3
  N3: WeMos_D1_Mini_Relay_Shield_V1.NC, L1.pin2

notes:
  12v AC
  GND
