# Fritzing sketch oficina_led_verm (saved by Fritzing 0.9.3b)
breadboards: 1

parts:
  Part2 = Arduino Uno (Rev3) - ICSP
  LED1 = LED - 3mm [color="Red (633nm)" package="3 mm [THT]"]
  R1 = Resistor [tolerance=±5% resistance=220 package="0402 [SMD]"]
  Part3 = Soil Moisture Sensor

nets:
  N1: Part2.A0, Part3.SIG
  5V: Part2.5V, Part3.VCC
  N2: Part2.D13/SCK, LED1.anode
  GND: Part2.GND, R1.Pin_1, Part3.GND
  N3: LED1.cathode, R1.Pin_0
