# Fritzing sketch oficina_sens_umid (saved by Fritzing 0.9.3b)

parts:
  Part2 = Arduino Uno (Rev3) - ICSP
  Part3 = Soil Moisture Sensor

nets:
  N1: Part2.A0, Part3.SIG
  5V: Part2.5V, Part3.VCC
  GND: Part2.GND, Part3.GND
