# Fritzing sketch prototipo_lcd_esdi (saved by Fritzing 0.9.3b)
breadboards: 1

parts:
  Part1 = Arduino Nano (Rev3.0) (ICSP)
  Part2 = Soil Moisture Sensor
  PCB2 = RTC_DS1302_module
  WeMos_D1_Mini_Relay_Shield_V1 = WeMos D1 Mini Relay Shield V2
  Part3 = Soil Moisture Sensor

nets:
  GND: Part1.GND, Part2.GND, PCB2.GND, WeMos_D1_Mini_Relay_Shield_V1.G, Part3.GND
  N1: Part1.D4, WeMos_D1_Mini_Relay_Shield_V1.D3
  N2: Part1.D8, PCB2.RST
  N3: Part1.D9, PCB2.DAT
  N4: Part1.D10, PCB2.CLK
  5V: Part1.5V, Part2.VCC, PCB2.VCC, WeMos_D1_Mini_Relay_Shield_V1.5V
  N5: Part1.A0, Part2.SIG

custom parts:
  RTC_DS1302_module: Arduino module DS1302 SPI Real Time Clock
