# Fritzing sketch prototipo_v0.1_esdi (saved by Fritzing 0.9.3b)
breadboards: 1

parts:
  Part1 = Soil Moisture Sensor
  Part2 = Arduino Uno (Rev3) - ICSP
  WeMos_D1_Mini_Relay_Shield_V1 = WeMos D1 Mini Relay Shield V2
  L1 = Solenoid
  PCB2 = RTC_DS1302_module

nets:
  N1: Part1.SIG, Part2.A0
  GND: Part1.GND, Part2.GND, PCB2.GND
  VCC: Part1.VCC, Part2.5V, WeMos_D1_Mini_Relay_Shield_V1.5V, PCB2.VCC
  N2: Part2.D8, PCB2.RST
  N3: Part2.D9_PWM, PCB2.DAT
  N4: Part2.D10_PWM/SS, PCB2.CLK
  N5: Part2.D4, WeMos_D1_Mini_Relay_Shield_V1.D3
  N6: WeMos_D1_Mini_Relay_Shield_V1.NC, L1.pin2

notes:
  12v AC
  GND

custom parts:
  RTC_DS1302_module: Arduino module DS1302 SPI Real Time Clock
