# Fritzing sketch sens_umid_DIY (saved by Fritzing 0.9.3b)
breadboards: 1

parts:
  Part2 = Arduino Uno (Rev3) - ICSP
  Part3 = Soil Moisture Sensor
  R1 = Resistor [tolerance=±5% resistance=10k package=THT]

nets:
  N1: Part2.A0, Part3.SIG, R1.Pin_0
  N2: Part2.5V, R1.Pin_1
  GND: Part2.GND, Part3.GND
